// Logisim project Задание для 11 пр.circ as structural Verilog: 1 circuit, main circuit main
module main (
);

  wire and_2_out, and_3_out, and_5_out, and_6_out, and_8_out, clock_1_out, or_3_out, Q1, Q2;
  wire [0:0] and_1_out;
  wire [2:0] c_q, c_qn;
  wire [3:0] or_4_out;

  Clock clock_1 (.out(clock_1_out));
  D_Flip_Flop c (.clk(clock_1_out), .D(c_qn[0]), .Q(c_q[0]), .Qn(c_qn[0]), .en(1'b1));  // open: preset, reset
  and and_1 (and_1_out[0], c_qn[1], c_qn[0]);
  and and_2 (and_2_out, c_qn[2], c_qn[1], c_q[0]);
  or or_1 (Q1, and_2_out, and_3_out);
  and and_3 (and_3_out, c_q[1], c_qn[0]);
  D_Flip_Flop b (.clk(clock_1_out), .D(Q1), .Q(c_q[1]), .Qn(c_qn[1]), .en(1'b1));  // open: preset, reset
  and and_4 (or_4_out[3], c_qn[2], c_q[0]);
  and and_5 (and_5_out, c_q[2], c_qn[0]);
  or or_2 (Q2, and_5_out, and_6_out);
  and and_6 (and_6_out, c_q[1], c_q[0]);
  D_Flip_Flop a (.clk(clock_1_out), .D(Q2), .Q(c_q[2]), .Qn(c_qn[2]), .en(1'b1));  // open: preset, reset
  or or_3 (or_3_out, c_qn[1], c_q[0]);
  and and_7 (or_4_out[2], or_3_out, c_qn[2]);
  Hex_Digit_Display hex_digit_display_1 (.value({3'b000, and_1_out[0]}));  // open: dp
  and and_8 (and_8_out, c_qn[1], c_qn[0]);
  or or_4 (or_4_out[0], and_8_out, c_q[2]);
  Hex_Digit_Display hex_digit_display_2 (.value({or_4_out[3:2], 1'b0, or_4_out[0]}));  // open: dp
endmodule
