// Logisim project bmem.circ as structural Verilog: 1 circuit, main circuit bmem
module bmem (
  input  [5:0] in_1,
  output [29:0] out_2
);

  wire [31:30] rom_1_data;

  ROM #(.addrWidth(6), .dataWidth(32)) rom_1 (.addr(in_1), .data({rom_1_data, out_2}));  // open: sel

  // Notes on the sheet:
  //   contents of rom_1 (hex, n*v repeats v):
  //   fa51e0 1fad6e0 1fad540 1f84200 6e949c3 1fad620 1b27c9b a8d540 1f0889f 1f0c89f 1f22a20 1743e0 1f4111f
  //   1f213e0 e8c5c0 1f843e0 1fa5100 e8c620 1087e10 1928898 c93e4c 1151151 1e10bc3 18213e0 1f0bc3f
  //   3c270bc3 10f94e0 1f29c1f 1f29c00 11ad5c0 1f27e3f 2aa53e0 e9d5c0 447c00 13ad720 15ad7e0 1c213e0
  //   1dad6e0 ead6e0 109d300 1bad760 1dad7e0 421080 318000
endmodule
