// Logisim project mainCore.circ as structural Verilog: 1 circuit, main circuit main
module main (
  input  SList,
  input  GList,
  input  CodeLoad,
  input  [3:0] FOutput,
  input  [19:0] Pcode,
  input  FOutput1Bit,
  input  [3:0] CData,
  output [3:0] n4,
  output [3:0] n3,
  output [3:0] n2,
  output [29:0] b1,
  output [29:0] b8,
  output [3:0] n1,
  output [3:0] n0,
  output [29:0] b2,
  output [29:0] b9,
  output [29:0] b3,
  output [29:0] b10,
  output [29:0] b4,
  output [29:0] b11,
  output [29:0] b5,
  output [29:0] b12,
  output rs,
  output [29:0] b6,
  output [29:0] b13,
  output [29:0] b15,
  output [29:0] b18,
  output [29:0] b7,
  output [29:0] b14,
  output [15:0] E1,
  output [29:0] b16,
  output [29:0] b19,
  output [15:0] E2,
  output [15:0] E3,
  output [29:0] b17,
  output [29:0] b20,
  output [15:0] E4,
  output [3:0] Finput,
  output [15:0] Data1,
  output [15:0] Data2,
  output [15:0] Data3,
  output ErCode,
  output [15:0] Data4,
  output [2:0] out_44,
  output [3:0] CDir,
  output [3:0] CMax,
  output [3:0] CStep,
  output CSinhro
);

  wire comparator_1_eq, comparator_3_eq, not_1_out, or_1_out, or_2_out, or_3_out, or_10_out,
       \proverka22_1_правильность , proverka23_1_er, proverka23_1_ok, proverkachip21_1_out_5, s3;
  wire [3:0] or_9_out;
  wire [5:0] m1, m2, m3, m4, m5, m6, m7, m8, m9, m10, m11, m12, m13, m14, m15, m16, m17, m18, m19, m20;
  wire [6:0] s2;
  wire [11:0] adder_1_out, s1;
  wire [15:0] or_8_out, proverka22_1_out_5, proverkachip21_1_out_7;
  wire [19:19] controlled_buffer_2_out;
  wire [23:0] grndeltamem_1_out_2;

  Counter #(.width(7), .max('h7f)) counter_1 (
    .load(s3), .D(s2), .count(GList), .Q({n4[2:0], n3}), .clk(or_1_out), .clr(comparator_1_eq));  // open: carry
  or or_1 (or_1_out, GList, s3);
  Comparator #(.width(7), .mode("unsigned")) comparator_1 (
    .a({n4[2:0], n3}), .b(7'b0111101), .eq(comparator_1_eq));  // open: gt, lt
  assign s3 = not_1_out ? CodeLoad : 1'bz;  // Controlled_Buffer controlled_buffer_1
  assign {controlled_buffer_2_out[19], s2, s1} = not_1_out ? Pcode : 20'bz;  // Controlled_Buffer controlled_buffer_2
  Comparator #(.width(20), .mode("unsigned")) comparator_2 (.a(Pcode), .b(20'h3c697), .gt(ErCode));  // open: eq, lt
  grnMem2 grnmem2_1 (.in_1({n4[2:0], n3}), .out_2({m20[1:0], m15, m16, m17, m18, m19}));
  grnMem1 grnmem1_1 (.in_1({n4[2:0], n3}), .out_2(m20[5:2]));
  grnDeltaMem grndeltamem_1 (.in_1({n4[2:0], n3}), .out_2(grndeltamem_1_out_2));
  bmem bmem_1 (.in_1(m15), .out_2(b15));
  bmem bmem_2 (.in_1(m16), .out_2(b16));
  bmem bmem_3 (.in_1(m17), .out_2(b17));
  not not_1 (not_1_out, ErCode);
  bmem bmem_4 (.in_1(m18), .out_2(b18));
  bmem bmem_5 (.in_1(m19), .out_2(b19));
  bmem bmem_6 (.in_1(m20), .out_2(b20));
  or or_2 (or_2_out, SList, s3);
  or or_3 (or_3_out, GList, comparator_3_eq);
  Counter #(.width(12), .max('hfff)) counter_2 (
    .load(s3), .D(s1), .count(SList), .Q({n2, n1, n0}), .clk(or_2_out), .clr(or_3_out));  // open: carry
  or or_4 (rs, SList, GList, s3);
  Adder #(.width(12)) adder_1 (.a(grndeltamem_1_out_2[23:12]), .b({n2, n1, n0}), .out(adder_1_out));  // open: cin, cout
  Comparator #(.width(12), .mode("unsigned")) comparator_3 (
    .a({n2, n1, n0}), .b(grndeltamem_1_out_2[11:0]), .eq(comparator_3_eq));  // open: gt, lt
  stnMem3 stnmem3_1 (.in_1(adder_1_out), .out_2({m11[1:0], m12, m13, m14}));
  stnMem2 stnmem2_1 (.in_1(adder_1_out), .out_2({m6[3:0], m7, m8, m9, m10, m11[5:2]}));
  stnMem1 stnmem1_1 (.in_1(adder_1_out), .out_2({m1, m2, m3, m4, m5, m6[5:4]}));
  Clock clock_1 (.out(out_44[1]));
  bmem bmem_7 (.in_1(m1), .out_2(b1));
  bmem bmem_8 (.in_1(m2), .out_2(b2));
  bmem bmem_9 (.in_1(m3), .out_2(b3));
  bmem bmem_10 (.in_1(m4), .out_2(b4));
  bmem bmem_11 (.in_1(m5), .out_2(b5));
  bmem bmem_12 (.in_1(m6), .out_2(b6));
  bmem bmem_13 (.in_1(m7), .out_2(b7));
  proverka23 proverka23_1 (
    .iData(CData), .C(out_44[1]), .\Вариант (adder_1_out), .Ok(proverka23_1_ok), .\Напр (CDir),
    .\Макс (CMax), .\Шаг (CStep), .SinhroOut(CSinhro), .er(proverka23_1_er));
  proverkaChip21 proverkachip21_1 (
    .in_2(FOutput1Bit), .in_3(adder_1_out), .out_5(proverkachip21_1_out_5), .out_7(proverkachip21_1_out_7),
    .C(out_44[1]));  // open: out_4, out_6
  proverka22 proverka22_1 (
    .\Вариант (FOutput), .in_3(adder_1_out), .\Правильность (\proverka22_1_правильность ),
    .out_5(proverka22_1_out_5), .out_6(E2), .out_7(E3), .out_8(E4), .out_9(Finput), .out_10(Data1),
    .out_11(Data2), .out_12(Data3), .out_13(Data4), .C(out_44[1]));
  bmem bmem_14 (.in_1(m8), .out_2(b8));
  bmem bmem_15 (.in_1(m9), .out_2(b9));
  bmem bmem_16 (.in_1(m10), .out_2(b10));
  bmem bmem_17 (.in_1(m11), .out_2(b11));
  bmem bmem_18 (.in_1(m12), .out_2(b12));
  bmem bmem_19 (.in_1(m13), .out_2(b13));
  bmem bmem_20 (.in_1(m14), .out_2(b14));
  assign E1 = proverka22_1_out_5 | proverkachip21_1_out_7;  // OR_Gate or_5, 16 bits wide
  or or_6 (out_44[0], \proverka22_1_правильность , proverka23_1_ok, proverkachip21_1_out_5);
  or or_7 (out_44[2], proverka23_1_er, or_10_out);
  assign or_8_out = E4 | E3 | E2 | E1;  // OR_Gate or_8, 16 bits wide
  assign or_9_out = or_8_out[15:12] | or_8_out[11:8] | or_8_out[7:4] | or_8_out[3:0];  // OR_Gate or_9, 4 bits wide
  or or_10 (or_10_out, or_9_out[3], or_9_out[2], or_9_out[1], or_9_out[0]);

  assign n4[3] = 1'b0;

  // Notes on the sheet:
  //   граница личного кода
  //   граница групп
  //   Вариант
endmodule
