// Logisim project proverka21.circ as structural Verilog: 1 circuit, main circuit proverkaChip21
module proverkaChip21 (
  input  C,
  input  in_2,
  input  [11:0] in_3,
  output [3:0] out_4,
  output out_5,
  output [15:0] out_6,
  output [15:0] out_7
);

  wire and_1_out, and_2_out, counter_1_carry, d_ff_1_q, d_ff_1_qn, not_1_out;
  wire [15:0] controlled_buffer_1_out, shift_register_1_q0;

  Counter #(.width(4), .max('hf), .ongoal("stay")) counter_1 (
    .count(C), .Q(out_4), .carry(counter_1_carry), .clk(C));  // open: load, D, clr
  not not_1 (not_1_out, C);
  and and_1 (and_1_out, counter_1_carry, not_1_out);
  D_Flip_Flop d_ff_1 (.clk(C), .D(and_1_out), .Q(d_ff_1_q), .Qn(d_ff_1_qn));  // open: preset, en, reset
  and and_2 (and_2_out, d_ff_1_qn, C);
  ROM #(.addrWidth(12), .dataWidth(16)) rom_1 (.addr(in_3), .data(out_6));  // open: sel
  Shift_Register #(.length(16)) shift_register_1 (
    .shift(1'b1), .in(in_2), .clk(and_2_out), .q0(shift_register_1_q0[0]), .q1(shift_register_1_q0[1]),
    .q2(shift_register_1_q0[2]), .q3(shift_register_1_q0[3]), .q4(shift_register_1_q0[4]),
    .q5(shift_register_1_q0[5]), .q6(shift_register_1_q0[6]), .q7(shift_register_1_q0[7]),
    .q8(shift_register_1_q0[8]), .q9(shift_register_1_q0[9]), .q10(shift_register_1_q0[10]),
    .q11(shift_register_1_q0[11]), .q12(shift_register_1_q0[12]), .q13(shift_register_1_q0[13]),
    .q14(shift_register_1_q0[14]), .q15(shift_register_1_q0[15]));  // open: out, load, clr, d0, d1, d2, d3, d4, d5, d6, d7, d8, d9, d10, d11, d12, d13, d14, d15
  assign controlled_buffer_1_out = d_ff_1_q ? out_6 : 16'bz;  // Controlled_Buffer controlled_buffer_1
  Comparator #(.width(16)) comparator_1 (
    .a(controlled_buffer_1_out), .b(shift_register_1_q0), .eq(out_5));  // open: gt, lt
  assign out_7 = shift_register_1_q0 ^ controlled_buffer_1_out;  // XOR_Gate xor_1, 16 bits wide

  // Notes on the sheet:
  //   Вход логической функции
  //    (Номер варианта - 1) как двоичное 10ти разрядное число
  //   contents of rom_1 (hex, n*v repeats v):
  //   abc7 a79e b237 5ab7 9b1d 9979 733b 1bb3 9b5c 2777 b879 6774 a66d d639 1b97 ed55 b6dc 8977 6d56 b747
  //   2b6e e674 57ea cba9 3997 74de d4e5 7d38 6c3e e687 d4be 27d5 dcd4 6739 36e5 7a17 3e8e bc35 e5ce 7d16
  //   5e1b ccab 65eb db1c 4bc7 6277 5ec7 1cdd d237 3b47 8e77 363b 63b6 d5b3 d1e5 9a6d b61d 7d71 37ce 7c3b
  //   66b3 6b57 e669 6c3d 8e6b e9c5 9ee5 6677 7d53 e83e dc63 cd74 b95b 64e7 b8ce d6d1 d8dd 4cb7 a6e7 9acb
  //   4dc7 e83b 6667 4ce7 b5ba 2767 be95 bee1 31ee 57a5 e933 b86e dc5d 78b9 3d5d ed33 d9ec d369 7e45 68de
  //   aea7 4dce b6c6 72ad eca6 a36e e7a5 bde1 ccb6 3bd2 dc2e ede2 dba5 3d72 eb1a 3c9e 4b97 e4c7 5795 eaba
  //   ce3b 7d4d ce4e ab9d 69b7 a337 ed1b b95c 6b53 ba8e 7e78 7333 e9c6 c72d a2be dd4d 39b7 5657 734d 947b
  //   3e78 ea5c 1dd9 ab6a d687 13be 9ad5 d539 aabd bc5b ccec 9abc 36e9 19dd 9bcc 935d 9dae ea3a 43db d5d3
  //   3ba6 17cb 6a5e 9a77 dab3 ed8a e3c6 7bd4 b99e b2bb 98bd b87d 96ea ac5e 74e6 abd3 17c7 e6c7 6abb ce35
  //   963d ba97 8d5d ebaa eae4 e72a 8ee3 b6d1 cd6d b9b5 75b2 d5a3 c4dd a95d 9e4b 6b69 d953 7e1d 1677 eb95
  //   e4cb b2ab 39bd c9bd c66e 976a 5877 9a6b 45d7 77a1 a6be 973d de8b 2a7e e1d5 7e29 b5a7 bcd6 5b72 e761
  //   35ea 7aa7 e716 54d7 55da bb94 c9b5 63de 1eee bce3 7c1d b78e d39a 6aba 6d87 ade6 d5e1 dc5a 53eb 7caa
  //   5da5 39d9 6d71 e6e6 5d95 99bb e4d6 aae7 c17e 1dc7 da4e 2d57 7937 b574 35e9 4b3d edc4 d58b 3abe 97ac
  //   aeca ecb3 ada3 e56a 53ed 975e 365e b99b 5cbb 27bd 89de 6dc9 b539 b1d5 731d e877 4eea 7663 2e77 eb2e
  //   7857 1b9d 93e5 2797 ee96 375e eee4 abd1 b967 ec1b ab3a 667c 2e6e 1ece 7ae2 d723 5b3c 7c3d dae1 b38d
  //   5d57 a96d eae9 9ee2 93da ee1c 7969 791d de95 796c add5 6979 b4b9 d68b 547d d4cd cdad 4577 7d94 979b
  //   d547 1d67 c78e 51db 73a6 5dcb ce4d 6cdd dd2a 739d 93ed da5d e5cd 7735 eaae 2bb3 9ad9 b7e1 acb5 89d7
  //   35cb b7d8 3be9 bb13 a8db 57b6 e937 e3ca 49bd 2d3b d75a 7b4b b673 d3c3 b19d 3787 d8be b57c e2e5 daae
  //   9d97 5aae c5bc d67c 3379 3cec c6a7 7c5e c9b3 b6b8 a4de c17b e9ca a1be d2ea d197 d92e 7c76 ec97 ab36
  //   23bd 2e75 ce8d b1a7 db38 eb3a 667d c5b5 5b1b 7963 7d9c 2ebb 92b7 87a7 2be9 6bab 7de8 955e 3d8d b6e2
  //   c87e 9ae9 7715 bb61 665d e66b eee2 719d 39b9 d693 3e8d 6676 bda1 3abd ab6b e5b5 8d6b 9cd5 baae 7768
  //   655b b4e5 8ae7 bad3 a7da d6ba e9d1 5bd5 dd92 4b9d 27b9 b51d adaa 7a6e ad63 2bbb 1dec 765d 29bb b359
  //   7da2 3796 6b4b a4dd 1b5b 76ac 13dd acdc dd3c 7d13 e667 8eab 6cb5 e5e8 66de 3975 5756 795c 36a7 4d3d
  //   e59a b71a 5dad c5a7 e972 a35b 357e 1d5e 6b96 6e66 967a 4db3 bec3 cb2d 9be8 cdc7 7d1b 1dbc ab9e 953b
  //   7ea8 abb9 5a9e 77c6 8d57 d764 3d9b de17 3db4 66ce 587d 6ecc dc6e 7365 87e7 6a5b d9cd 754d c99e ee85
  //   979d 37b9 1767 7719 77a2 dad4 7727 5b1d dc79 c7a7 b297 9dab c5eb d1b5 7479 9ada 7ea9 d2ae b4ea a3ec
  //   337d 799e 66ba a3e7 58d7 b5a3 78ba 3d3b 65c7 45b7 d179 e973 557c 8ee9 7556 3b6d 7dc1 95dc cd75 dbb4
  //   7e66 ab3d aee5 71b6 5b76 ed43 aba6 63b9 d91b 357b 3177 b7c8 9dd8 db51 9eda 6ed9 3e5d ab27 7179 33de
  //   6de4 3e8b 5797 ecea ea4b e3e6 3ea3 e927 bc73 d87c d333 36dd 7a8b a37d 47d7 a3e5 d978 3567 7367 bce5
  //   b2e3 9eab 3b3d 3b96 3dcb 4777 a6ba bd9c 769d 7363 54be d4c7 b72e 277b c3ab 7bc1 8e67 6ba7 c7d9 6b75
  //   d6d3 ab7c caec 3ecc 19be bd16 43bb 75a9 b387 4d79 ce1b d963 877c 6bb2 971d 7c99 e5ea 9e87 97c3 89ee
  //   ea4e 6cd7 66dc b3ea e857 dc7a c65e 3cb5 663d b9d3 b9d1 bb91 ba78 b74e 4bb5 d565 95b3 1e9b b66a cd7c
  //   89e7 bad6 bab5 7bc6 b2a7 936d 7b64 56d9 ee3a 6dc5 5766 8e73 2bd3 71d5 6ec9 74cb 33e7 3cd6 95ed 6e4e
  //   5dae 1d97 d93e 9d65 a5bb aae6 dd4e d6ad e477 ee92 ead2 8bbc b93a cb53 c97d 71db dae9 a6cd dd34 eb8d
  //   7731 de51 78e7 a55d e475 b33c ad5a d758 4a7e 59da 7e32 e9dc a667 72be d5b1 be16 d45b ee36 e8be 7acd
  //   e8b7 4c77 dbca 3cbd e2ce e5d6 87ed b4cd b4d5 e2de da5a 5977 57da 5be1 747e e666 bb19 6b72 1bdb 1d7c
  //   b7e4 2c7d 678e 137b a99d 4ebd ed99 bd6a e17a e997 be25 37b8 25de 7756 b9b6 91de 91eb b3ac 9576 c95b
  //   e25d 7d36 89bb 74b6 5e2d d83e 6bb5 b2ec d713 36d3 657d 9ed8 7567 9c7b ab65 bca9 a4ed b4e6 2d3e 17be
  //   9dcd dc95 7a6c e137 1ad7 47db e5b4 4e3d e52e 8eee b5e1 de5c 7876 bd56 dd9c a67e 736a 75b3 2d67 1a7e
  //   6abc ebd1 ba33 e65d 9bdc 9747 267b 355d 76ca b8d7 e5c6 7566 5a76 bd35 73cc 63cb 7ec2 6d63 c79b 7636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
  //   Входной набор для функции со счетчика
  //   Результат оценки 1 - правильно
  //   Диагностика ошибок
endmodule
