// Logisim project proverka22.circ as structural Verilog: 1 circuit, main circuit proverka22
module proverka22 (
  input  C,
  input  [3:0] \Вариант ,
  input  [11:0] in_3,
  output \Правильность ,
  output [15:0] out_5,
  output [15:0] out_6,
  output [15:0] out_7,
  output [15:0] out_8,
  output [3:0] out_9,
  output [15:0] out_10,
  output [15:0] out_11,
  output [15:0] out_12,
  output [15:0] out_13
);

  wire proverkachip21_1_out_5, proverkachip21_2_out_5, proverkachip21_3_out_5, proverkachip21_4_out_5;
  wire [11:0] adder_1_out, adder_2_out, adder_3_out;

  Adder #(.width(12)) adder_1 (.a(in_3), .b(12'h1), .out(adder_1_out));  // open: cin, cout
  Adder #(.width(12)) adder_2 (.a(adder_1_out), .b(12'h1), .out(adder_2_out));  // open: cin, cout
  Adder #(.width(12)) adder_3 (.a(adder_2_out), .b(12'h1), .out(adder_3_out));  // open: cin, cout
  proverkaChip21 proverkachip21_1 (
    .in_2(\Вариант [3]), .in_3(in_3), .out_5(proverkachip21_1_out_5), .out_7(out_5), .C(C), .out_6(out_10));  // open: out_4
  proverkaChip21 proverkachip21_2 (
    .in_2(\Вариант [2]), .in_3(adder_1_out), .out_5(proverkachip21_2_out_5), .out_7(out_6), .C(C),
    .out_6(out_11));  // open: out_4
  proverkaChip21 proverkachip21_3 (
    .in_2(\Вариант [1]), .in_3(adder_2_out), .out_5(proverkachip21_3_out_5), .out_7(out_7), .C(C),
    .out_6(out_12));  // open: out_4
  proverkaChip21 proverkachip21_4 (
    .in_2(\Вариант [0]), .in_3(adder_3_out), .out_4(out_9), .out_5(proverkachip21_4_out_5), .out_7(out_8),
    .C(C), .out_6(out_13));
  and and_1 (\Правильность , proverkachip21_1_out_5, proverkachip21_2_out_5, proverkachip21_3_out_5, proverkachip21_4_out_5);

  // Notes on the sheet:
  //   Вход логической функции
  //   4-х ядерный процессор :)
  //   Входной набор для функции
  //   Ошибка 1
  //   Ошибка 2
  //   Ошибка 3
  //   Ошибка 4
  //   var
  //   var+1
  //   var+2
  //   var+3
endmodule
