// Logisim project proverka23.circ as structural Verilog: 1 circuit, main circuit proverka23
module proverka23 (
  input  C,
  input  [3:0] iData,
  input  [11:0] \Вариант ,
  output SinhroOut,
  output Ok,
  output er,
  output [3:0] \Напр ,
  output [3:0] \Макс ,
  output [3:0] \Шаг 
);

  wire _1, and_1_out, and_2_out, and_3_out, and_5_out, and_6_out, comparator_1_eq, comparator_1_lt,
       comparator_2_eq, comparator_2_gt, comparator_2_lt, controlled_buffer_1_out, d_ff_1_qn, d_ff_2_qn,
       d_ff_3_q, nand_1_out, not_1_out, or_1_out, or_2_out, t_ff_1_q, t_ff_1_qn;
  wire [3:0] register_1_q, unycout_1_value;
  wire [4:0] counter_1_q;

  and and_1 (and_1_out, iData[3], iData[2], iData[1], iData[0]);
  assign controlled_buffer_1_out = or_1_out ? C : 1'bz;  // Controlled_Buffer controlled_buffer_1
  or or_1 (or_1_out, and_1_out, not_1_out);
  not not_1 (not_1_out, and_1_out);
  and and_2 (and_2_out, controlled_buffer_1_out, ~comparator_1_eq);  // AND_Gate
  Counter #(.width(5), .max('h1f), .ongoal("stay"), .trigger("falling")) counter_1 (
    .count(1'b1), .Q(counter_1_q), .clk(and_2_out));  // open: load, D, carry, clr
  Comparator #(.width(5), .mode("unsigned")) comparator_1 (
    .a(counter_1_q), .b(5'b10001), .eq(comparator_1_eq), .lt(comparator_1_lt));  // open: gt
  cntmv cntmv_1 (.in_1(\Вариант ), .out_2({\Напр , \Макс , \Шаг }));
  and and_3 (and_3_out, 1'b1, t_ff_1_qn);
  T_Flip_Flop t_ff_1 (
    .clk(controlled_buffer_1_out), .T(and_3_out), .Q(t_ff_1_q), .Qn(t_ff_1_qn));  // open: preset, reset, en
  and and_4 (SinhroOut, comparator_1_lt, _1, controlled_buffer_1_out);
  Register #(.width(4), .trigger("low")) register_1 (
    .D(iData), .en(1'b1), .Q(register_1_q), .clk(SinhroOut));  // open: clr
  D_Flip_Flop #(.trigger("falling")) d_ff_1 (
    .clk(controlled_buffer_1_out), .D(t_ff_1_q), .Q(_1), .Qn(d_ff_1_qn));  // open: preset, en, reset
  Hex_Digit_Display hex_digit_display_1 (.value(register_1_q));  // open: dp
  Hex_Digit_Display hex_digit_display_2 (.value(unycout_1_value));  // open: dp
  UnyCout unycout_1 (
    .Step(\Шаг ), .Dir(\Напр [0]), .Cin(SinhroOut), .Max(\Макс ), .Value(unycout_1_value), .wr(and_5_out),
    .Start(iData));
  and and_5 (and_5_out, t_ff_1_q, d_ff_1_qn);
  Comparator #(.width(4)) comparator_2 (
    .a(register_1_q), .b(unycout_1_value), .gt(comparator_2_gt), .eq(comparator_2_eq), .lt(comparator_2_lt));
  or or_2 (or_2_out, comparator_2_lt, comparator_2_eq, comparator_2_gt);
  nand nand_1 (nand_1_out, comparator_2_eq, d_ff_2_qn);
  D_Flip_Flop #(.trigger("falling")) d_ff_2 (
    .clk(SinhroOut), .D(nand_1_out), .Qn(d_ff_2_qn), .en(_1));  // open: Q, preset, reset
  D_Flip_Flop #(.trigger("falling")) d_ff_3 (
    .clk(SinhroOut), .D(or_2_out), .Q(d_ff_3_q), .en(_1));  // open: Qn, preset, reset
  and and_6 (and_6_out, d_ff_3_q, comparator_1_eq);
  assign Ok = and_6_out ? d_ff_2_qn : 1'bz;  // Controlled_Buffer controlled_buffer_2
  not not_2 (er, Ok);
endmodule
