// Logisim project stnMem1.circ as structural Verilog: 1 circuit, main circuit stnMem1
module stnMem1 (
  input  [11:0] in_1,
  output [31:0] out_2
);

  ROM #(.addrWidth(12), .dataWidth(32)) rom_1 (.addr(in_1), .data(out_2));  // open: sel

  // Notes on the sheet:
  //   contents of rom_1 (hex, n*v repeats v):
  //   b2cb2c00 b2cb0040 b2cb2c04 b2cb2c05 b2cb2cb0 b2c0ce2d b2cb2cb0 b2cb2cb0 b2cb2cb0 b2c29000 b2cb2c29
  //   b2c2ce29 b2cb0c00 b2cb0c21 b2cb2cb2 b2cb2c34 b2cb2c34 b2cb0f15 b2cb2cb2 b2c4400c b2cb1114 b1139039
  //   b2cb2cb2 b2cb2cb2 b2cb2c50 b2cb1501 9*b2cb0201 5*b2c08040 b2cb2c00 b2cb2c00 b2cb2cb0 b2cb2cb0
  //   b2c0ce45 b2cb2cb2 b2cb2c0d b2cb2cb0 b2cb2cb0 b2cb2cb0 b2cb2c30 b2cb2cb2 b2cb1000 b2cb2cb2 b2cb2c41
  //   b2cb2c44 b2cb2cb1 b2cb2cb2 b2cb2cb2 b2cb2c48 b2cb2c49 b2cb154d b2cb2cb2 b2cb2cb2 16*b2c08040
  //   b2cb0138 b2cb2cb0 b2cb2cb0 b2cb2c20 b2cb2c20 b2cb2cb2 b2cb0a38 b2cb2cb0 b2cb2cb2 b2cb2c2c b2cb0b38
  //   b2cb2c30 b2cb2cb2 b2cb0d38 b2cb0f15 b2cb1001 b2cb2cb2 b2c4852c b2cb2cb2 b2cb1500 b2cb2c60 b2cb2cb2
  //   b2cb2c60 b2cb2cb2 b2cb2cb1 15*b2c08040 b2cb2c00 b0061b40 b2cb2cb0 b2cb2cb0 b2cb2c05 c01cc00 b2cb2cb2
  //   b2cb2c10 b2cb2c10 b2cb2cb0 b2c1c00c b2cb2cb2 b2cb2cb0 b2cb0a20 b2cb2cb0 b2cb2cb2 b2cb0c21 b2cb2cb0
  //   b0e0ce40 b2cb1000 b2cb2cb1 b2cb2cb2 b2cb2c50 b2cb2cb1 b2cb2cb1 b2cb2cb1 b2cb1814 13*b2c08040
  //   b2cb000c b2cb2cb2 b2cb2c08 b2cb2cb2 b2cb2c15 b2cb0714 b2cb2cb2 b2cb2cb0 b2cb2cb0 b2cb2c28 4*b2cb2cb2
  //   b2cb2cb0 b2cb2c30 b2cb2cb0 b2cb0c4d b2cb2c34 b2cb2c3c b2cb2c44 b2cb2cb1 b2cb2cb1 b2cb1238 b2cb1414
  //   b2cb2c50 b2c6052c 13*b2c08040 b2cb2cb0 b2cb2cb0 b2cb0138 b2cb0138 b2c08834 b2c08e14 b2cb2c08
  //   b2cb2c08 b2cb0400 b2c10540 b2cb2cb2 b2cb2cb2 b2cb2cb2 b2cb0c14 b2cb0c15 b2cb2cb2 b2cb2cb0 b2c3ce1c
  //   b2cb2c40 b2cb2cb1 b2cb2c40 b2cb2cb1 b2cb2cb1 b2cb2c45 b2cb2cb2 b2cb2c60 14*b2c08040 111344 b2cb2cb0
  //   b2cb2c04 b2cb2cb2 b2c0c815 b2cb2cb0 b2cb0439 b2cb2cb0 b2cb2cb2 b2cb2c28 b2cb2c2c b2cb2cb2 b2cb2cb2
  //   b2cb2cb0 b2cb2cb0 b2cb2c31 b2cb2cb0 b2cb2cb2 b2cb2cb2 b2cb2cb0 b2cb1114 b2cb1115 b2cb2cb1 b2cb2c49
  //   b2c50041 b2cb1715 b2cb2c60 13*b2c08040 b2cb2c04 b2c04e34 b2cb2cb0 b2cb2cb0 b2cb2cb2 b2cb2cb0
  //   b2cb2cb0 b2cb2cb0 b2cb2cb2 b2cb2cb2 b2cb2cb0 b2cb2c29 b2cb2cb0 b2cb0c01 b2cb0d15 b2cb2cb2 b2cb0f2c
  //   b2cb2cb0 b2cb2cb2 b2cb2cb1 b2cb2cb1 b2cb2c45 b2cb2c49 b2cb2cb1 b2c08040 15*b0201020 b2cb0009
  //   b2cb2c04 b2cb2cb0 b2cb2c08 b2cb2cb2 b0239039 b2cb2c09 b2cb2c0c b2cb2cb2 b2cb2cb2 b2cb2c1c b2cb2cb0
  //   b2cb2cb0 b2cb2c20 b2cb2cb0 b2cb0a00 b2cb2cb0 b2cb0a4c b2cb2cb0 b2cb2cb0 b2cb2cb2 b2cb2cb0 b2cb2cb1
  //   b2cb2cb2 b2cb2c55 b2cb2cb1 b2cb2cb1 b2cb2cb2 b2cb2cb1 b2cb2cb2 b2cb2c64 9*b0201020 b2cb2cb0 b2cb2cb2
  //   b2cb2cb0 b2cb2cb0 b2cb2cb2 b2cb2c0d b2cb2cb2 b2cb2cb2 b2cb2c20 b2cb2cb2 b2cb2cb0 b2c28e2c b2cb2c28
  //   b2cb2cb0 b2cb0a40 b2cb2cb2 b2cb2cb0 b2cb2cb0 b2cb2cb2 b2cb2cb0 b2cb2cb2 b2c3d020 b2cb2c44 b2cb1100
  //   b1114c21 b2cb2c44 b2cb2cb2 b2cb2cb2 b2cb2cb2 b2cb2cb1 b2cb2c60 9*b0201020 b2cb2c04 b2cb2c08 b2cb2c08
  //   b2cb2cb2 b2cb2c0c b2cb2cb0 b2cb2cb0 b2cb2cb2 b2cb0700 b2cb083c b2c28008 b2cb2cb0 b2cb2c28 b2cb2c28
  //   b2cb2cb0 b2cb2cb0 b2cb2cb2 b2cb2cb0 b2cb2cb2 b2cb2c30 b2c30849 b2cb2cb2 b2cb2cb2 b2cb2c3c b2cb2cb2
  //   b2cb2c40 b2cb2cb2 b2cb2c44 b2cb2cb1 b1238c01 b2cb2cb2 b171507d 8*b0201020 b2cb000c b2cb2cb2 b2c01530
  //   b2c04040 b2cb0138 b2cb2cb0 b2cb2cb2 b2cb2cb0 b2cb2c10 b2cb2c10 b2cb2cb2 b2cb0700 b2cb0700 b2c20200
  //   b2cb2cb0 b2c28e18 b2cb2cb0 b2cb2c29 b2cb2cb2 b2cb2cb0 b2cb2cb0 3002cb01 b2cb2cb0 b2cb2c3c b2cb2cb1
  //   b2cb2c41 b2cb2c44 b2cb2cb1 b1148040 b2cb1148 b2cb2cb2 b2cb1715 b2cb2c60 7*b0201020 b2cb2c00 b2cb2c04
  //   b2cb2cb2 b2cb2c04 b2cb0138 b2cb2c05 b2cb2cb2 b2cb2cb0 b2cb0400 b2cb2c10 b2cb0415 b2cb2cb0 b2cb0701
  //   b2cb2cb0 b2cb2cb2 b2cb2cb0 b2cb0e28 b2cb2c38 b2cb2cb0 44020440 b2cb2c44 b2cb2cb1 b2cb1221 b2cb2cb2
  //   b2cb2cb1 b2cb2c4c b2cb2cb2 b2cb2cb1 b2cb1614 b2cb2c60 b2cb2cb1 9*b0201020 111b40 4025000 b2c04e0c
  //   b2c04e34 b2c04e40 b2cb0201 b2cb2cb2 b2c093b0 b2cb2cb2 b2cb2cb0 b2cb2c0c b2cb2cb0 b2cb2cb2 b2cb2c0d
  //   b2cb2cb2 b2cb2c15 b2cb2cb0 b2cb2c21 b2cb2cb0 b2cb0c00 b2cb2cb0 b2cb0e2c b2cb2cb0 b2cb2cb1 b2cb2c44
  //   b2cb2cb2 b2cb2cb2 b2cb2cb1 b1214b14 b2cb2c49 b2cb2cb2 b2cb2cb2 b2cb2cb2 7*b0201020 b2cb2c00 b2cb2cb0
  //   b0201120 b2cb2cb2 b2cb2cb0 b2cb2c0c ce41f5c b2cb0340 b2cb2cb2 b2cb2cb2 b2cb0700 b2cb2cb2 b2cb2cb2
  //   b2cb0a38 b2cb0a39 b2cb2c28 b2cb0a40 b2cb2cb2 b2cb2cb0 b2c2df44 b2cb2cb2 b2cb2cb0 b2cb2c3c b2cb2c44
  //   b2cb2cb1 b2cb2cb2 b2c60545 b2cb2c64 12*b0201020 b2cb2cb2 b2cb0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
endmodule
