// Logisim project stnMem2.circ as structural Verilog: 1 circuit, main circuit stnMem2
module stnMem2 (
  input  [11:0] in_1,
  output [31:0] out_2
);

  ROM #(.addrWidth(12), .dataWidth(32)) rom_1 (.addr(in_1), .data(out_2));  // open: sel

  // Notes on the sheet:
  //   contents of rom_1 (hex, n*v repeats v):
  //   d0c048a2 2971450 52df28e0 34053571 215049f1 30483561 440e1862 72db10d1 82dc7d13 c01014d2 31107d83
  //   220e34e0 338c1443 500b2182 cb0c3901 54521503 85400803 240e45f3 c4130563 2c028e0 c14d2152 720d44a2
  //   c45238b0 c45b34a3 54101494 d4d23 9*200352b 5*800d4ac8 d1103994 f4882851 100b0183 30041881 31004050
  //   cb034cb2 344524d3 a4cb00a3 c00a0103 c00c1443 e40e1ce0 c3871503 c00700d3 c4130563 f1c03561 852dc1
  //   120c38d3 c45b44e1 cb116d71 540554e0 e40534a3 1ce28e0 c60860a3 cb2c7982 16*800d4ac8 301244a0 13830171
  //   714b14d3 200d14d2 201914d2 c28040f0 200b14d2 a38a0101 c2c538d3 848220d3 101148e0 28e0851 c3135483
  //   239114b3 5082ce0 238244a2 cb107c13 535220d3 c5004083 d0181422 40400d3 c6050974 54053054 c60860a3
  //   f28e08b1 9*800d4ac8 6*800d4ac9 300b00a3 44d011b1 101000d3 14cd0d31 360c00d3 300c1523 c0d32df1
  //   531714d2 e3083434 53441503 e40e10d7 c1c020a2 808034a2 cb0c20d4 a4130cb3 c29349c2 1ce0401 c3884451
  //   e10d20a3 c00700d3 130840d3 cb114d02 510e40e0 538c7ca3 74cc00a3 800100d3 228e3cb7 13*800d4ac9 10600d7
  //   c0452df1 40400d7 c08e2ca3 440530e0 93481042 c20200d3 a00700a3 a3874c13 e2c46d81 c28e4062 c28e6052
  //   c29078a3 cb0a4c72 b20f0123 40a0107 c4cc20d3 1ce04e1 828e2c01 852dc1 a01020d2 12c010a3 138a38b3
  //   300b00a3 439014d2 82c83cf3 e3053561 13*800d4ac9 3444051 121078a3 301214d2 d1004174 e0d00043 238444a2
  //   e2ce1083 e40e34a3 22c54982 509f34d6 c20200d3 cb0b2112 c2d32883 614220a2 1cb20a2 cb0c2062 f2174c32
  //   435f28e0 e0ce1883 38628e0 e30034e0 120258e0 130840d3 360d20a3 c5455903 3034cb3 8*800d4ac9 6*800d4aca
  //   4923903 10106d81 44a00a3 c04e24a3 120420d3 414d2113 39814d2 700c4cb2 c2801de4 e3455cd6 49334e0
  //   cb2cb2c2 cb0b7023 c00b0153 c0120851 34520142 f01538c3 c3c54903 cb0f38f3 f40e3570 d34828e0 c814d2
  //   14c104e4 32920103 53841ce1 14c2112 545200a3 13*800d4aca 4114ca3 401014d2 33914850 40026c43 c1130483
  //   52d720d7 600a6cf3 71411c51 c20200d3 cb084401 a3842103 31ce08b1 b3833822 14c4ca3 72120092 c34e7cd3
  //   e48d20a3 f39200f3 cb104d14 114b2191 12043903 24052ca3 182851 24cc00a3 800d4aca 15*352b218 c14d2
  //   2ca0103 14d73450 52c85ca2 c08b0113 234828e0 614d2 1c42050 cb0400d3 c15054e0 54040e0 70150107
  //   714d58e0 b7085c50 82dc7d13 a41f58a2 a00d6c32 441f0961 a4cb70f2 b6d100a3 c30840a2 f14b7122 14d500d3
  //   c4453083 34120050 714a2931 74c10103 c5d33c83 74d700b2 c6134135 540120d2 9*352b218 139500d3 c0503822
  //   14c72c01 14d06d52 c08e2ca3 348a3822 c15420c3 c18400d3 200d14d2 c2020182 a21114b1 544d20a3 e40e4801
  //   a3923822 9714d2 c2934801 b38320d3 c0120851 c3455c01 d38220a3 c3c540b3 b14f44a2 9714d2 b14d28e0
  //   701148d3 a2df10d1 c4934001 c4d000a3 c5c540d6 814c1523 541148d1 9*352b218 e0c05c50 548e60a2 e2c53522
  //   c0c04881 e2ce0883 414c00a2 52c84451 cb054183 408e40d0 f38b2123 a00744a2 a0103ce0 84082cb3 841e6083
  //   a3907c32 a41e5ca3 c2c538d3 b14e34e0 c2c834d2 40a0103 39400d3 cb0f00d2 c3c54903 b01238d3 c3ce2df1
  //   e3003574 c4402043 a08e4163 130840d3 814244a2 c4cc1503 234828e0 7*352b218 352b219 30548e0 c00a38f7
  //   511500d3 d0123822 30126d01 239038d2 c0c02ca3 338b20a3 e2935c01 e3444ca3 cb044cb3 b38c44a2 f41310d3
  //   d34828e0 a00f20d4 508d20a3 a38c0103 2023813 c2933d63 a7d02073 b3810171 80150403 c4d01552 549354e0
  //   38628e0 331f3561 3004161 138b38f3 e1130561 e7cd3822 c45b44e1 1420126 f21034e0 7*352b219 301438d3
  //   24c00d3 c0452df1 e0c400d3 b7d720d3 2120050 c08044a0 201178d2 220414d2 509f48a2 1427cd2 615148a3
  //   501014d2 a38114d2 c28e59e0 b3810171 83581422 a4cd70a3 f01538c3 54c38d3 e28e2ca3 20100122 538c2103
  //   c48a0171 238b4523 b1c54931 cb142194 50010103 b28e08d1 54053054 84cc44a2 9*352b219 54c00d3 c0c52c42
  //   49b4050 401014d2 e1132c83 54136083 cb021500 46cab074 cb026ce3 271e60a3 3464d03 30100174 cb0338b7
  //   340100d3 cb2c1003 420c2883 808034e0 140014b7 c00b6d52 d0d36050 d3820174 535714d2 f4c30171 108540b3
  //   22107ca3 cb1114c2 c44b0023 20100113 c4d00123 39420c3 c49b58a2 cb2cb153 c61340c0 7*352b219 400c14d2
  //   10124d23 b71714d2 c08e24d3 30024083 e4014cd3 a38244a2 80ce41c1 c1433903 cb060032 f41f0c01 cb0720d2
  //   cb074c13 200b14d2 38b2152 e40e48a3 44e48a2 cb2c2c00 b1411441 a38244a2 c3085451 c2151450 e30834e0
  //   810e40e0 138b38d2 c48530a2 238f00b3 54010171 12*352b219 cb2c00a4 854047 540c00a3 3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
endmodule
