// Logisim project Подготовка к экзамену.circ as structural Verilog: 1 circuit, main circuit main
module main (
  input  R,
  input  E,
  input  Et,
  input  in_4,
  input  E_2,
  input  Et_2,
  input  [1:0] in_7,
  input  [1:0] in_8,
  input  [1:0] in_9,
  input  [1:0] in_10,
  input  [1:0] in_11,
  input  [1:0] in_12,
  input  [1:0] in_13,
  input  [1:0] in_14,
  input  R_2,
  input  R_3,
  input  E_3,
  input  E_4,
  input  Et_3,
  input  Et_4,
  input  E_5,
  input  Et_5,
  input  in_23,
  input  R_4,
  input  in_25,
  input  X0,
  input  X1,
  input  E_6,
  input  X0_2,
  input  X1_2,
  input  E_7,
  input  Cin,
  input  A,
  input  B,
  output out_35,
  output out_36,
  output out_37,
  output out_38,
  output out_39,
  output out_40,
  output out_41,
  output out_42
);

  wire and_1_out, and_2_out, and_4_out, C_2_out, C_out, clock_1_out, clock_2_out, clock_3_out,
       decoder_1_out0, decoder_1_out1, decoder_1_out2, decoder_1_out3, decoder_2_out0, decoder_2_out1,
       decoder_2_out2, decoder_2_out3, multiplexer_2_out, multiplexer_3_out, multiplexer_4_out,
       multiplexer_6_out, not_1_out, not_2_out, not_3_out, not_4_out, or_1_out, or_2_out, or_3_out, R_2_out,
       R_out, t0_3_q, t0_3_qn, T0_5_q, T0_q, T0_qn, t1_3_q, T1_4_q, xor_1_out, xor_2_out;
  wire [1:0] clock_4_out, multiplexer_1_out, multiplexer_5_out, multiplexer_7_out, multiplexer_8_out,
       priority_encoder_1_out, T0_2_q, T0_4_q, undriven;
  wire [5:2] T1_qn;

  Clock clock_1 (.out(clock_1_out));
  Clock clock_2 (.out(clock_2_out));
  and and_1 (and_1_out, T1_qn[4], T0_q);
  T_Flip_Flop #(.trigger("falling")) T0 (
    .clk(clock_1_out), .T(Et), .Q(T0_q), .Qn(T0_qn), .reset(or_1_out), .en(E));  // open: preset
  or or_1 (or_1_out, and_1_out, R);
  T_Flip_Flop #(.trigger("falling")) T0_2 (
    .clk(clock_2_out), .T(Et_3), .Q(T0_2_q[0]), .reset(R_2), .en(E_3));  // open: Qn, preset
  T_Flip_Flop #(.trigger("falling")) T1 (
    .clk(T0_q), .T(Et), .Q(T1_qn[4]), .Qn(T1_qn[2]), .reset(or_1_out), .en(E));  // open: preset
  Multiplexer #(.select(2), .width(2)) multiplexer_1 (
    .in0(in_7), .in1(in_9), .in2(in_11), .in3(in_13), .out(multiplexer_1_out), .sel(T0_2_q), .en(E_3));
  // Probe on multiplexer_1_out
  T_Flip_Flop #(.trigger("falling")) T1_2 (
    .clk(T0_2_q[0]), .T(Et_3), .Q(T0_2_q[1]), .reset(R_2), .en(E_3));  // open: Qn, preset
  Clock clock_3 (.out(clock_3_out));
  Button u_R (.out(R_out));
  xor xor_1 (xor_1_out, B, A);
  not not_1 (not_1_out, xor_1_out);
  and and_2 (and_2_out, B, A);
  or or_2 (or_2_out, B, A);
  and and_3 (T1_qn[5], T0_qn, T1_qn[2]);
  Clock clock_4 (.out(clock_4_out[0]));
  T_Flip_Flop #(.trigger("falling")) t0_3 (
    .clk(clock_3_out), .T(1'b1), .Q(t0_3_q), .Qn(t0_3_qn), .reset(or_3_out), .en(1'b1));  // open: preset
  Multiplexer #(.disabled(0), .enable("false")) multiplexer_2 (
    .in0(t0_3_q), .in1(t0_3_qn), .out(multiplexer_2_out), .sel(in_25));
  LED S (.in(multiplexer_3_out));
  LED Cout (.in(multiplexer_4_out));
  Multiplexer #(.disabled(0), .enable("false")) multiplexer_3 (
    .in0(xor_1_out), .in1(not_1_out), .out(multiplexer_3_out), .sel(Cin));
  Multiplexer #(.disabled(0), .enable("false")) multiplexer_4 (
    .in0(and_2_out), .in1(or_2_out), .out(multiplexer_4_out), .sel(Cin));
  // Probe on {T1_qn[5:4], 1'b1, T1_qn[2], T1_qn[4], T1_qn[2]}
  T_Flip_Flop #(.trigger("falling")) T (
    .clk(clock_4_out[0]), .T(Et_4), .Q(clock_4_out[1]), .reset(R_3), .en(E_4));  // open: Qn, preset
  T_Flip_Flop #(.trigger("falling")) t1_3 (
    .clk(multiplexer_2_out), .T(1'b1), .Q(t1_3_q), .reset(or_3_out), .en(1'b1));  // open: Qn, preset
  or or_3 (or_3_out, R_out, and_4_out);
  // Probe on multiplexer_5_out
  Multiplexer #(.select(2), .width(2)) multiplexer_5 (
    .in0(in_8), .in1(in_10), .in2(in_12), .in3(in_14), .out(multiplexer_5_out), .sel(clock_4_out), .en(E_4));
  and and_4 (and_4_out, clock_3_out, t0_3_qn, t1_3_q);
  Clock C (.out(C_out));
  not not_2 (not_2_out, xor_2_out);
  Button u_R_2 (.out(R_2_out));
  T_Flip_Flop #(.trigger("falling")) T0_4 (
    .clk(C_2_out), .T(Et_5), .Q(T0_4_q[0]), .reset(R_4), .en(E_5));  // open: Qn, preset
  Clock C_2 (.out(C_2_out));
  D_Flip_Flop #(.trigger("falling")) T1_4 (
    .clk(C_out), .D(multiplexer_6_out), .Q(T1_4_q), .en(E_2), .reset(R_2_out));  // open: Qn, preset
  Multiplexer #(.disabled(0)) multiplexer_6 (
    .in0(xor_2_out), .in1(not_2_out), .out(multiplexer_6_out), .sel(in_4), .en(E_2));
  xor xor_2 (xor_2_out, T1_4_q, T0_5_q);
  T_Flip_Flop #(.trigger("falling")) T1_5 (
    .clk(T0_4_q[0]), .T(Et_5), .Q(T0_4_q[1]), .reset(R_4), .en(E_5));  // open: Qn, preset
  T_Flip_Flop #(.trigger("falling")) T0_5 (
    .clk(C_out), .T(Et_2), .Q(T0_5_q), .reset(R_2_out), .en(E_2));  // open: Qn, preset
  not not_3 (not_3_out, in_23);
  Decoder #(.select(2), .disabled(0)) decoder_1 (
    .out0(decoder_1_out0), .out1(decoder_1_out1), .out2(decoder_1_out2), .out3(decoder_1_out3), .sel(T0_4_q),
    .en(not_3_out));
  Decoder #(.select(2), .disabled(0)) decoder_2 (
    .out0(decoder_2_out0), .out1(decoder_2_out1), .out2(decoder_2_out2), .out3(decoder_2_out3), .sel(T0_4_q),
    .en(in_23));
  Priority_Encoder #(.select(2)) priority_encoder_1 (
    .in0(decoder_1_out0), .in1(decoder_1_out1), .in2(decoder_1_out2), .in3(decoder_1_out3),
    .out(priority_encoder_1_out));  // open: gs, en_out, en_in
  // Probe on multiplexer_7_out
  Multiplexer #(.select(2), .width(2), .disabled(0)) multiplexer_7 (
    .in0(2'b11), .in1(2'b10), .in2(2'b01), .in3(2'b10), .out(multiplexer_7_out),
    .sel(priority_encoder_1_out), .en(E_5));
  Priority_Encoder #(.select(2)) priority_encoder_2 (
    .in0(decoder_2_out3), .in1(decoder_2_out2), .in2(decoder_2_out1), .in3(decoder_2_out0),
    .out(priority_encoder_1_out));  // open: gs, en_out, en_in
  // Probe on multiplexer_8_out
  Multiplexer #(.select(2), .width(2), .disabled(0)) multiplexer_8 (
    .in0(2'b11), .in1(2'b10), .in2(2'b01), .in3(2'b10), .out(multiplexer_8_out), .sel(undriven));  // open: en
  Multiplexer #(.select(2), .disabled(0)) multiplexer_9 (
    .in0(1'b1), .in1(1'b0), .in2(1'b0), .in3(1'b0), .out(out_35), .sel({X1, X0}), .en(E_6));
  Multiplexer #(.select(2), .disabled(0)) multiplexer_10 (
    .in0(1'b0), .in1(1'b1), .in2(1'b0), .in3(1'b0), .out(out_37), .sel({X1, X0}), .en(E_6));
  Multiplexer #(.select(2), .disabled(0)) multiplexer_11 (
    .in0(1'b0), .in1(1'b0), .in2(1'b1), .in3(1'b0), .out(out_39), .sel({X1, X0}), .en(E_6));
  Multiplexer #(.select(2), .disabled(0)) multiplexer_12 (
    .in0(1'b0), .in1(1'b0), .in2(1'b0), .in3(1'b1), .out(out_41), .sel({X1, X0}), .en(E_6));
  not not_4 (not_4_out, X0_2);
  Multiplexer #(.disabled(0)) multiplexer_13 (.in0(not_4_out), .in1(1'b0), .out(out_36), .sel(X1_2), .en(E_7));
  Multiplexer #(.disabled(0)) multiplexer_14 (.in0(X0_2), .in1(1'b0), .out(out_38), .sel(X1_2), .en(E_7));
  Multiplexer #(.disabled(0)) multiplexer_15 (.in0(1'b0), .in1(not_4_out), .out(out_40), .sel(X1_2), .en(E_7));
  Multiplexer #(.disabled(0)) multiplexer_16 (.in0(1'b0), .in1(X0_2), .out(out_42), .sel(X1_2), .en(E_7));

  // Notes on the sheet:
  //   I вариант (мне нравится)
  //   II вариант (мне не нравится)
endmodule
